// Logisim project Circuitos A.circ as structural Verilog
module ULA (
  input  a,
  input  CarryIn,
  input  b,
  input  Op1,
  input  Op2,
  output S,
  output CarryOut
);

  wire adder_1_out, and_1_out, or_1_out;

  and and_1 (and_1_out, a, b);
  or or_1 (or_1_out, a, b);
  Adder #(.width(1)) adder_1 (.a(a), .b(b), .out(adder_1_out), .cin(CarryIn), .cout(CarryOut));
  Multiplexer #(.select(2), .enable("false")) multiplexer_1 (
    .in0(and_1_out), .in1(or_1_out), .in2(adder_1_out), .in3(1'b0), .out(S), .sel({Op1, Op2}));
endmodule

module ULA_Sub (
  input  CarryIn,
  input  a,
  input  b,
  input  Op1,
  input  B_inv,
  input  Op2,
  output S,
  output CarryOut
);

  wire adder_1_out, and_1_out, multiplexer_1_out, not_1_out, or_1_out;

  not not_1 (not_1_out, b);
  Multiplexer #(.enable("false")) multiplexer_1 (.in0(not_1_out), .in1(b), .out(multiplexer_1_out), .sel(B_inv));
  and and_1 (and_1_out, a, b);
  or or_1 (or_1_out, a, b);
  Adder #(.width(1)) adder_1 (.a(a), .b(multiplexer_1_out), .out(adder_1_out), .cin(CarryIn), .cout(CarryOut));
  Multiplexer #(.select(2), .enable("false")) multiplexer_2 (
    .in0(and_1_out), .in1(or_1_out), .in2(adder_1_out), .out(S), .sel({Op1, Op2}));  // open: in3
endmodule
