// Logisim project EP_02_AC2.circ as structural Verilog: 6 circuits, main circuit main
module main (
  input  Ci,
  input  a,
  input  b,
  input  OP0,
  input  Bi,
  input  OP1,
  output S0,
  output Co
);

  ULA ula_1 (.a(a), .b(b), .S(S0), .Ci(Ci), .Binvert(Bi), .Co(Co), .OP1(OP1), .OP0(OP0));
endmodule

module ULA (
  input  Ci,
  input  a,
  input  b,
  input  OP1,
  input  OP0,
  input  Binvert,
  output S,
  output Co
);

  wire and_1_out, multiplexer_1_out, not_1_out, not_2_out, or_1_out, somador_1_s0;

  not not_1 (not_1_out, b);
  Multiplexer #(.enable("false")) multiplexer_1 (.in0(b), .in1(not_1_out), .out(multiplexer_1_out), .sel(Binvert));
  and and_1 (and_1_out, a, multiplexer_1_out);
  or or_1 (or_1_out, a, multiplexer_1_out);
  not not_2 (not_2_out, a);
  Somador somador_1 (.c0(Ci), .a0(a), .b0(multiplexer_1_out), .s0(somador_1_s0), .c0_2(Co));
  Multiplexer #(.select(2), .enable("false")) multiplexer_2 (
    .in0(and_1_out), .in1(or_1_out), .in2(not_2_out), .in3(somador_1_s0), .out(S), .sel({OP1, OP0}));
endmodule

module Somador (
  input  c0,
  input  a0,
  input  b0,
  output s0,
  output c0_2
);

  wire meio_somador_1_c, meio_somador_1_s, meio_somador_2_c;

  Meio_Somador meio_somador_1 (.a1(c0), .a2(a0), .s(meio_somador_1_s), .c(meio_somador_1_c));
  Meio_Somador meio_somador_2 (.a1(meio_somador_1_s), .a2(b0), .s(s0), .c(meio_somador_2_c));
  or or_1 (c0_2, meio_somador_2_c, meio_somador_1_c);

  // Notes on the sheet:
  //   c0: pull=up
endmodule

module Meio_Somador (
  input  a1,
  input  a2,
  output s,
  output c
);

  xor xor_1 (s, a1, a2);
  and and_1 (c, a2, a1);
endmodule

module ULA_de_4_bits (
  input  b3,
  input  b2,
  input  b1,
  input  b0,
  input  a3,
  input  a2,
  input  a1,
  input  a0,
  input  OP1,
  input  OP0,
  input  Binvert,
  output s0,
  output s1,
  output s2,
  output s3,
  output Cout
);

  wire ula_1_co, ula_2_co, ula_3_co;

  ULA ula_1 (.a(a0), .b(b0), .S(s0), .Ci(Binvert), .Binvert(Binvert), .Co(ula_1_co), .OP1(OP1), .OP0(OP0));
  ULA ula_2 (.a(a1), .b(b1), .S(s1), .Ci(ula_1_co), .Binvert(Binvert), .Co(ula_2_co), .OP1(OP1), .OP0(OP0));
  ULA ula_3 (.a(a2), .b(b2), .S(s2), .Ci(ula_2_co), .Binvert(Binvert), .Co(ula_3_co), .OP1(OP1), .OP0(OP0));
  ULA ula_4 (.a(a3), .b(b3), .S(s3), .Ci(ula_3_co), .Binvert(Binvert), .Co(Cout), .OP1(OP1), .OP0(OP0));
endmodule

module ULA_74LS181 (
  input  [3:0] a,
  input  [3:0] b,
  input  [3:0] Chave,
  output [3:0] S
);

  wire [3:0] and_1_out, and_2_out, and_3_out, nand_1_out, nor_1_out, not_1_out, not_2_out, not_3_out,
       not_4_out, not_5_out, or_1_out, or_2_out, or_3_out, xnor_1_out, xor_1_out;

  assign not_1_out = ~a;  // NOT_Gate not_1, 4 bits wide
  assign not_2_out = ~a;  // NOT_Gate not_2, 4 bits wide
  assign not_3_out = ~b;  // NOT_Gate not_3, 4 bits wide
  assign not_4_out = ~b;  // NOT_Gate not_4, 4 bits wide
  assign not_5_out = ~a;  // NOT_Gate not_5, 4 bits wide
  assign nor_1_out = ~(a | b);  // NOR_Gate nor_1, 4 bits wide
  assign and_1_out = not_2_out & b;  // AND_Gate and_1, 4 bits wide
  assign nand_1_out = ~(a & b);  // NAND_Gate nand_1, 4 bits wide
  assign xor_1_out = a ^ b;  // XOR_Gate xor_1, 4 bits wide
  assign and_2_out = a & not_4_out;  // AND_Gate and_2, 4 bits wide
  assign or_1_out = not_5_out | b;  // OR_Gate or_1, 4 bits wide
  assign xnor_1_out = ~(a ^ b);  // XNOR_Gate xnor_1, 4 bits wide
  assign and_3_out = a & b;  // AND_Gate and_3, 4 bits wide
  assign or_2_out = a | ~b;  // OR_Gate or_2, 4 bits wide
  assign or_3_out = b | a;  // OR_Gate or_3, 4 bits wide
  Multiplexer #(.select(4), .width(4), .enable("false")) multiplexer_1 (
    .in0(not_1_out), .in1(nor_1_out), .in2(and_1_out), .in3(4'b0000), .in4(nand_1_out), .in5(not_3_out),
    .in6(xor_1_out), .in7(and_2_out), .in8(or_1_out), .in9(xnor_1_out), .in10(b), .in11(and_3_out),
    .in12(4'b1111), .in13(or_2_out), .in14(or_3_out), .in15(a), .out(S), .sel(Chave));
endmodule
