// Logisim project EP_01_AC2.circ as structural Verilog: 3 circuits, main circuit main
module main (
  input  a0,
  input  b0,
  input  Ci0,
  input  a1,
  input  b1,
  input  a2,
  input  b2,
  input  a3,
  input  b3,
  output s0,
  output s1,
  output s2,
  output s3,
  output Co
);

  wire somador_1_co, somador_2_co, somador_3_co;

  Somador somador_1 (.a0(a0), .b0(b0), .Ci(Ci0), .s0(s0), .Co(somador_1_co));
  Somador somador_2 (.a0(a1), .b0(b1), .Ci(somador_1_co), .s0(s1), .Co(somador_2_co));
  Somador somador_3 (.a0(a2), .b0(b2), .Ci(somador_2_co), .s0(s2), .Co(somador_3_co));
  Somador somador_4 (.a0(a3), .b0(b3), .Ci(somador_3_co), .s0(s3), .Co(Co));

  // Notes on the sheet:
  //   a3 a2 a1 a0
  //   0 0 0 1
  //   s3 s2 s1 s0
  //   0 1 1 0
  //   b3 b2 b1 b0
  //   0 1 0 1
  //   A Soma dos primeiros dígitos da minha matrícula
  //   (1 + 5), resulta em 6, o que comprova que o somador funciona
endmodule

module Meio_Somador (
  input  a0,
  input  b0,
  output Soma,
  output Carry
);

  and and_1 (Carry, a0, b0);
  xor xor_1 (Soma, a0, b0);
endmodule

module Somador (
  input  a0,
  input  b0,
  input  Ci,
  output s0,
  output Co
);

  wire Meio_Somador_2_carry, Meio_Somador_carry, Meio_Somador_soma;

  Meio_Somador Meio_Somador (.a0(a0), .b0(b0), .Soma(Meio_Somador_soma), .Carry(Meio_Somador_carry));
  Meio_Somador Meio_Somador_2 (.a0(Meio_Somador_soma), .b0(Ci), .Soma(s0), .Carry(Meio_Somador_2_carry));
  or or_1 (Co, Meio_Somador_carry, Meio_Somador_2_carry);
endmodule
