// Logisim project Multiplicador de 3 bits.circ as structural Verilog: 4 circuits, main circuit main
module main (
  input  a2,
  input  a1,
  input  a0,
  input  b2,
  input  b1,
  input  b0,
  output s0,
  output s1,
  output s2,
  output s3,
  output s4,
  output s5
);

  Multiplicador multiplicador_1 (
    .a2(a2), .a1(a1), .a0(a0), .b2(b2), .b1(b1), .b0(b0), .s0(s0), .s1(s1), .s2(s2), .s3(s3), .s4(s4), .s5(s5));
endmodule

module Somador (
  input  a0,
  input  b0,
  input  Ci,
  output s0,
  output Co
);

  wire meio_somador_1_cout, meio_somador_1_soma, meio_somador_2_cout;

  Meio_Somador meio_somador_1 (.a(a0), .b(b0), .Soma(meio_somador_1_soma), .Cout(meio_somador_1_cout));
  Meio_Somador meio_somador_2 (.a(meio_somador_1_soma), .b(Ci), .Soma(s0), .Cout(meio_somador_2_cout));
  or or_1 (Co, meio_somador_1_cout, meio_somador_2_cout);
endmodule

module Meio_Somador (
  input  a,
  input  b,
  output Soma,
  output Cout
);

  xor xor_1 (Soma, a, b);
  and and_1 (Cout, a, b);
endmodule

module Multiplicador (
  input  a2,
  input  a1,
  input  a0,
  input  b2,
  input  b1,
  input  b0,
  output s0,
  output s1,
  output s2,
  output s3,
  output s4,
  output s5
);

  wire and_2_out, and_3_out, and_4_out, and_5_out, and_6_out, and_7_out, and_8_out, and_9_out, somador_1_co,
       somador_2_s0, somador_3_co, somador_3_s0, somador_5_co, somador_6_co;

  and and_1 (s0, b0, a0);
  and and_2 (and_2_out, b0, a1);
  and and_3 (and_3_out, b1, a0);
  and and_4 (and_4_out, b0, a2);
  and and_5 (and_5_out, b1, a1);
  and and_6 (and_6_out, b2, a0);
  and and_7 (and_7_out, b1, a2);
  and and_8 (and_8_out, b2, a1);
  and and_9 (and_9_out, b2, a2);
  Somador somador_1 (.a0(and_2_out), .b0(and_3_out), .Ci(1'b0), .s0(s1), .Co(somador_1_co));
  Somador somador_2 (.a0(and_4_out), .b0(and_5_out), .Ci(somador_1_co), .s0(somador_2_s0), .Co(and_8_out));
  Somador somador_3 (.a0(and_7_out), .b0(and_8_out), .Ci(and_8_out), .s0(somador_3_s0), .Co(somador_3_co));
  Somador somador_4 (.a0(somador_3_co), .b0(and_9_out), .Ci(somador_6_co), .s0(s4), .Co(s5));
  Somador somador_5 (.a0(somador_2_s0), .b0(and_6_out), .Ci(1'b0), .s0(s2), .Co(somador_5_co));
  Somador somador_6 (.a0(somador_3_s0), .b0(1'b0), .Ci(somador_5_co), .s0(s3), .Co(somador_6_co));
endmodule
